// Logisim project crcfull.circ as structural Verilog: 1 circuit, main circuit main
module main (
  input  Input_1,
  input  Input_2,
  input  Input_3,
  output Output_1
);

  wire and_1_out, d_ff_1_q, d_ff_2_q, d_ff_3_q, d_ff_4_q, d_ff_5_q, d_ff_6_q, d_ff_7_q, d_ff_8_q, d_ff_9_q,
       d_ff_10_q, d_ff_11_q, d_ff_12_q, d_ff_13_q, d_ff_14_q, d_ff_15_q, not_1_out, xor_1_out, xor_2_out,
       xor_3_out;

  xor xor_1 (xor_1_out, and_1_out, Input_2);
  D_Flip_Flop d_ff_1 (.D(xor_1_out), .clk(Input_3), .Q(d_ff_1_q));  // open: Qn, preset, reset
  D_Flip_Flop d_ff_2 (.D(d_ff_1_q), .clk(Input_3), .Q(d_ff_2_q));  // open: Qn, preset, reset
  D_Flip_Flop d_ff_3 (.D(d_ff_2_q), .clk(Input_3), .Q(d_ff_3_q));  // open: Qn, preset, reset
  D_Flip_Flop d_ff_4 (.D(d_ff_3_q), .clk(Input_3), .Q(d_ff_4_q));  // open: Qn, preset, reset
  D_Flip_Flop d_ff_5 (.D(d_ff_4_q), .clk(Input_3), .Q(d_ff_5_q));  // open: Qn, preset, reset
  D_Flip_Flop d_ff_6 (.D(xor_2_out), .clk(Input_3), .Q(d_ff_6_q));  // open: Qn, preset, reset
  xor xor_2 (xor_2_out, and_1_out, d_ff_5_q);
  D_Flip_Flop d_ff_7 (.D(d_ff_6_q), .clk(Input_3), .Q(d_ff_7_q));  // open: Qn, preset, reset
  D_Flip_Flop d_ff_8 (.D(d_ff_7_q), .clk(Input_3), .Q(d_ff_8_q));  // open: Qn, preset, reset
  D_Flip_Flop d_ff_9 (.D(d_ff_8_q), .clk(Input_3), .Q(d_ff_9_q));  // open: Qn, preset, reset
  D_Flip_Flop d_ff_10 (.D(d_ff_9_q), .clk(Input_3), .Q(d_ff_10_q));  // open: Qn, preset, reset
  D_Flip_Flop d_ff_11 (.D(d_ff_10_q), .clk(Input_3), .Q(d_ff_11_q));  // open: Qn, preset, reset
  D_Flip_Flop d_ff_12 (.D(d_ff_11_q), .clk(Input_3), .Q(d_ff_12_q));  // open: Qn, preset, reset
  xor xor_3 (xor_3_out, and_1_out, d_ff_12_q);
  D_Flip_Flop d_ff_13 (.D(xor_3_out), .clk(Input_3), .Q(d_ff_13_q));  // open: Qn, preset, reset
  and and_1 (and_1_out, not_1_out, Output_1);
  D_Flip_Flop d_ff_14 (.D(d_ff_13_q), .clk(Input_3), .Q(d_ff_14_q));  // open: Qn, preset, reset
  D_Flip_Flop d_ff_15 (.D(d_ff_14_q), .clk(Input_3), .Q(d_ff_15_q));  // open: Qn, preset, reset
  not not_1 (not_1_out, Input_1);
  D_Flip_Flop d_ff_16 (.D(d_ff_15_q), .clk(Input_3), .Q(Output_1));  // open: Qn, preset, reset
endmodule
